# Fritzing sketch hydrophonics shield (saved by Fritzing 0.7.10b)
perfboards: 1

parts:
  IC1 = ULN2003A [package="DIP16 [THT]"]
  Arduino_Ethernet_Shield1 = Arduino Ethernet Shield
  R2 = Resistor [tolerance=±5% resistance=10k package=THT]
  R3 = Resistor [tolerance=±5% resistance=10k package=THT]
  RHT1 = Humidity and Temperature Sensor RHT03
  R1 = Resistor [tolerance=±5% resistance=33 package=THT]
  SCT_013-000 = Inductor [package="400 mil [THT]"]  # not connected
  C1 = Electrolytic Capacitor [capacitance=10µF package="100 mil [THT, electrolytic]"]
  R4 = Resistor [tolerance=±5% resistance=10k package=THT]
  K1 = Relay [part_number=FRS1B-S package=THT]
  IC2 = DS1307 [package=THT]
  32_768_KHz = CRYSTAL - kHz [frequency="32 kHz"]
  DC_Power1 = DC Power [voltage=5]
  U1 = mystery part, 4 pins [chip_label=moisture]
  U2 = mystery part, 6 pins [chip_label=PH]

nets:
  N1: IC1.In_1, Arduino_Ethernet_Shield1.D8
  N2: IC1.In_2, Arduino_Ethernet_Shield1.D7
  N3: IC1.In_3, Arduino_Ethernet_Shield1.D6
  N4: IC1.In_4, Arduino_Ethernet_Shield1.D5
  N5: IC1.In_5, Arduino_Ethernet_Shield1.SS
  N6: IC1.In_6, Arduino_Ethernet_Shield1.D3
  GND: IC1.0V, Arduino_Ethernet_Shield1.GND, R3.Pin_1, RHT1.GND_1, C1.-, IC2.0V, DC_Power1.GND, U1.pin1, U2.pin3
  +5V: IC1.COM_-_Common, Arduino_Ethernet_Shield1.+5V, R2.Pin_0, RHT1.Vcc, R4.Pin_0, K1.B, IC2.+V, U1.pin2, U2.pin4
  N7: IC1.Out_1, K1.A
  N8: Arduino_Ethernet_Shield1.D2, RHT1.Data-signal, R4.Pin_1
  N9: Arduino_Ethernet_Shield1.D1TX, U2.pin2
  N10: Arduino_Ethernet_Shield1.D0RX, U2.pin1
  N11: Arduino_Ethernet_Shield1.A0, R1.Pin_1
  N12: Arduino_Ethernet_Shield1.A1, U1.pin4
  N13: Arduino_Ethernet_Shield1.A4, IC2.SDA_-_I2C_Data
  N14: Arduino_Ethernet_Shield1.A5, IC2.SCL_-_I2C_Clock
  N15: R2.Pin_1, R3.Pin_0, R1.Pin_0, C1.+
  N16: IC2.X1_-_Crystal, 32_768_KHz.pin_1
  N17: IC2.X2_-_Crystal, 32_768_KHz.pin_0
  N18: IC2.Vbat_-_Backup_Supply, DC_Power1.V+
